// Logisim project Lab1_Chips.circ as structural Verilog: 1 circuit, main circuit main
module main (
  input  A,
  input  B,
  input  C,
  input  D,
  output F
);

  wire n7404_1_pin2, n7408_1_pin3, n7408_1_pin11;

  _7404 u_7404_1 (
    .pin1(B), .pin2(n7404_1_pin2));  // open: pin3, pin4, pin5, pin6, pin13, pin12, pin11, pin10, pin9, pin8
  _7408 u_7408_1 (
    .pin1(D), .pin2(C), .pin3(n7408_1_pin3), .pin13(D), .pin12(n7404_1_pin2), .pin11(n7408_1_pin11));  // open: pin4, pin5, pin6, pin10, pin9, pin8
  _7432 u_7432_1 (
    .pin1(n7408_1_pin11), .pin2(n7408_1_pin3), .pin3(F));  // open: pin4, pin5, pin6, pin13, pin12, pin11, pin10, pin9, pin8
endmodule
