// Logisim project Circuit_1.circ as structural Verilog: 1 circuit, main circuit main
module main (
  input  C1,
  input  C0,
  input  R,
  output M1,
  output M0,
  output A
);

  wire nand_1_out, nand_2_out, nand_3_out, nand_4_out, nand_5_out, nand_7_out, nand_8_out, nand_9_out,
       not_1_out, not_2_out, not_3_out, not_4_out, not_5_out, not_6_out, not_7_out, not_8_out, not_9_out;

  not not_1 (not_1_out, C0);
  not not_2 (not_2_out, C0);
  not not_3 (not_3_out, C1);
  not not_4 (not_4_out, C0);
  not not_5 (not_5_out, R);
  not not_6 (not_6_out, C1);
  not not_7 (not_7_out, C0);
  nand nand_1 (nand_1_out, not_1_out, R);
  nand nand_2 (nand_2_out, not_2_out, not_3_out);
  nand nand_3 (nand_3_out, not_4_out, R);
  nand nand_4 (nand_4_out, C0, not_5_out);
  nand nand_5 (nand_5_out, not_6_out, not_7_out);
  not not_8 (not_8_out, nand_2_out);
  nand nand_6 (M0, nand_3_out, nand_4_out);
  not not_9 (not_9_out, nand_5_out);
  nand nand_7 (nand_7_out, nand_1_out, C1);
  nand nand_8 (nand_8_out, R, not_8_out);
  nand nand_9 (nand_9_out, not_9_out, R);
  not not_10 (A, nand_9_out);
  nand nand_10 (M1, nand_7_out, nand_8_out);
endmodule
