// Logisim project Circuit_2.circ as structural Verilog: 1 circuit, main circuit main
module main (
  input  A,
  input  B,
  input  C,
  input  D,
  output F
);

  wire nor_1_out, nor_2_out, nor_3_out, nor_4_out, nor_5_out, nor_6_out, nor_7_out, nor_8_out, nor_9_out,
       nor_10_out, nor_11_out, not_1_out, not_2_out;

  not not_1 (not_1_out, A);
  nor nor_1 (nor_1_out, A, B);
  nor nor_2 (nor_2_out, A, C);
  nor nor_3 (nor_3_out, not_1_out, B);
  nor nor_4 (nor_4_out, nor_2_out, nor_2_out);
  nor nor_5 (nor_5_out, nor_3_out, nor_3_out);
  not not_2 (not_2_out, D);
  nor nor_6 (nor_6_out, nor_4_out, D);
  nor nor_7 (nor_7_out, nor_5_out, not_2_out);
  nor nor_8 (nor_8_out, nor_1_out, nor_6_out);
  nor nor_9 (nor_9_out, nor_7_out, C);
  nor nor_10 (nor_10_out, nor_8_out, nor_8_out);
  nor nor_11 (nor_11_out, nor_9_out, nor_9_out);
  nor nor_12 (F, nor_10_out, nor_11_out);
endmodule
