// Logisim project Circuit_3.circ as structural Verilog: 1 circuit, main circuit main
module main (
  input  A,
  input  B,
  input  C,
  input  D,
  output F
);

  wire n7402_1_pin1, n7402_1_pin2, n7402_1_pin4, n7402_1_pin12, n7402_2_pin1, n7402_2_pin2, n7402_2_pin4,
       n7402_2_pin12, n7402_3_pin2, n7402_3_pin3, n7402_3_pin13, n7404_1_pin8, n7404_1_pin12;

  _7404 u_7404_1 (
    .pin13(A), .pin12(n7404_1_pin12), .pin9(D), .pin8(n7404_1_pin8));  // open: pin1, pin2, pin3, pin4, pin5, pin6, pin11, pin10
  _7402 u_7402_1 (
    .pin1(n7402_1_pin1), .pin2(n7402_1_pin2), .pin3(n7404_1_pin8), .pin4(n7402_1_pin4), .pin5(n7402_1_pin1),
    .pin6(C), .pin13(n7402_1_pin2), .pin12(n7402_1_pin12), .pin11(n7402_1_pin12), .pin10(n7402_1_pin12),
    .pin9(n7404_1_pin12), .pin8(B));
  _7402 u_7402_2 (
    .pin1(n7402_2_pin1), .pin2(n7402_2_pin2), .pin3(D), .pin4(n7402_2_pin4), .pin5(B), .pin6(A),
    .pin13(n7402_2_pin2), .pin12(n7402_2_pin12), .pin11(n7402_2_pin12), .pin10(n7402_2_pin12), .pin9(C),
    .pin8(A));
  _7402 u_7402_3 (
    .pin1(F), .pin2(n7402_3_pin2), .pin3(n7402_3_pin3), .pin4(n7402_3_pin3), .pin5(n7402_1_pin4),
    .pin6(n7402_1_pin4), .pin13(n7402_3_pin13), .pin12(n7402_2_pin1), .pin11(n7402_2_pin4),
    .pin10(n7402_3_pin2), .pin9(n7402_3_pin13), .pin8(n7402_3_pin13));
endmodule
