// Logisim project 4b_adder.circ as structural Verilog: 3 circuits, main circuit four_bit_adder
module four_bit_adder (
  input  A3,
  input  A2,
  input  A1,
  input  A0,
  input  B3,
  input  B2,
  input  B1,
  input  B0,
  output F3,
  output F2,
  output F1,
  output F0,
  output C
);

  wire full_adder_2_c, full_adder_3_c, full_adder_4_c;

  Full_Adder full_adder_1 (.A(A3), .B(B3), .Cin(full_adder_2_c), .S(F3), .C(C));
  Full_Adder full_adder_2 (.A(A2), .B(B2), .Cin(full_adder_3_c), .S(F2), .C(full_adder_2_c));
  Full_Adder full_adder_3 (.A(A1), .B(B1), .Cin(full_adder_4_c), .S(F1), .C(full_adder_3_c));
  Full_Adder full_adder_4 (.A(A0), .B(B0), .S(F0), .C(full_adder_4_c));  // open: Cin
endmodule

module Half_Adder (
  input  A,
  input  B,
  output S,
  output C
);

  and and_1 (C, A, B);
  xor xor_1 (S, A, B);
endmodule

module Full_Adder (
  input  A,
  input  B,
  input  Cin,
  output S,
  output C
);

  wire half_adder_1_c, half_adder_1_s, half_adder_2_c;

  Half_Adder half_adder_1 (.A(A), .B(B), .S(half_adder_1_s), .C(half_adder_1_c));
  Half_Adder half_adder_2 (.A(half_adder_1_s), .B(Cin), .S(S), .C(half_adder_2_c));
  or or_1 (C, half_adder_2_c, half_adder_1_c);
endmodule
