// Logisim project 4bit_alu_sample.circ as structural Verilog: 1 circuit, main circuit fourbit_alu
module fourbit_alu (
  input  [3:0] A,
  input  [3:0] B,
  input  [1:0] S,
  output C,
  output alu3,
  output alu2,
  output alu1,
  output alu0
);

  wire four_bit_adder_1_f0, four_bit_adder_1_f1, four_bit_adder_1_f2, four_bit_adder_1_f3, four_bit_and_1_f0,
       four_bit_and_1_f1, four_bit_and_1_f2, four_bit_and_1_f3, four_bit_not_1_f0, four_bit_not_1_f1,
       four_bit_not_1_f2, four_bit_not_1_f3, four_bit_or_1_f0, four_bit_or_1_f1, four_bit_or_1_f2,
       four_bit_or_1_f3;

  four_bit_NOT four_bit_not_1 (
    .A3(A[3]), .A2(A[2]), .A1(A[1]), .A0(A[0]), .F3(four_bit_not_1_f3), .F2(four_bit_not_1_f2),
    .F1(four_bit_not_1_f1), .F0(four_bit_not_1_f0));
  four_bit_OR four_bit_or_1 (
    .A3(A[3]), .A2(A[2]), .A1(A[1]), .A0(A[0]), .B3(B[3]), .B2(B[2]), .B1(B[1]), .B0(B[0]),
    .F3(four_bit_or_1_f3), .F2(four_bit_or_1_f2), .F1(four_bit_or_1_f1), .F0(four_bit_or_1_f0));
  four_bit_AND four_bit_and_1 (
    .A3(A[3]), .A2(A[2]), .A1(A[1]), .A0(A[0]), .B3(B[3]), .B2(B[2]), .B1(B[1]), .B0(B[0]),
    .F3(four_bit_and_1_f3), .F2(four_bit_and_1_f2), .F1(four_bit_and_1_f1), .F0(four_bit_and_1_f0));
  four_bit_adder four_bit_adder_1 (
    .A3(A[3]), .A2(A[2]), .A1(A[1]), .A0(A[0]), .B3(B[3]), .B2(B[2]), .B1(B[1]), .B0(B[0]),
    .F3(four_bit_adder_1_f3), .F2(four_bit_adder_1_f2), .F1(four_bit_adder_1_f1), .F0(four_bit_adder_1_f0),
    .C(C));
  Multiplexer #(.select(2)) multiplexer_1 (
    .in0(four_bit_not_1_f3), .in1(four_bit_or_1_f3), .in2(four_bit_and_1_f3), .in3(four_bit_adder_1_f3),
    .out(alu3), .sel(S));
  Multiplexer #(.select(2)) multiplexer_2 (
    .in0(four_bit_not_1_f2), .in1(four_bit_or_1_f2), .in2(four_bit_and_1_f2), .in3(four_bit_adder_1_f2),
    .out(alu2), .sel(S));
  Multiplexer #(.select(2)) multiplexer_3 (
    .in0(four_bit_not_1_f1), .in1(four_bit_or_1_f1), .in2(four_bit_and_1_f1), .in3(four_bit_adder_1_f1),
    .out(alu1), .sel(S));
  Multiplexer #(.select(2)) multiplexer_4 (
    .in0(four_bit_not_1_f0), .in1(four_bit_or_1_f0), .in2(four_bit_and_1_f0), .in3(four_bit_adder_1_f0),
    .out(alu0), .sel(S));
endmodule
