// Logisim project ALU.circ as structural Verilog: 1 circuit, main circuit main
module main (
  input  [3:0] A,
  input  [3:0] B,
  output [3:0] F
);

  four_bit_adder four_bit_adder_1 (
    .A3(A[0]), .A2(A[1]), .A1(A[2]), .A0(A[3]), .B3(B[0]), .B2(B[1]), .B1(B[2]), .B0(B[3]), .F3(F[0]),
    .F2(F[1]), .F1(F[2]), .F0(F[3]));  // open: C
endmodule
