// Logisim project ALU_components.circ as structural Verilog: 3 circuits, main circuit four_bit_OR
module four_bit_OR (
  input  A3,
  input  A2,
  input  A1,
  input  A0,
  input  B3,
  input  B2,
  input  B1,
  input  B0,
  output F3,
  output F2,
  output F1,
  output F0
);

  or or_1 (F3, A3, B3);
  or or_2 (F2, A2, B2);
  or or_3 (F1, A1, B1);
  or or_4 (F0, A0, B0);
endmodule

module four_bit_AND (
  input  A3,
  input  A2,
  input  A1,
  input  A0,
  input  B3,
  input  B2,
  input  B1,
  input  B0,
  output F3,
  output F2,
  output F1,
  output F0
);

  and and_1 (F3, A3, B3);
  and and_2 (F2, A2, B2);
  and and_3 (F1, A1, B1);
  and and_4 (F0, A0, B0);
endmodule

module four_bit_NOT (
  input  A3,
  input  A2,
  input  A1,
  input  A0,
  output F3,
  output F2,
  output F1,
  output F0
);

  not not_1 (F3, A3);
  not not_2 (F2, A2);
  not not_3 (F1, A1);
  not not_4 (F0, A0);
endmodule
