// Logisim project VCVS.circ as structural Verilog: 6 circuits, main circuit main
module main (
  input  X,
  input  Y,
  input  Z,
  input  [3:0] A_in,
  input  I2,
  input  I1,
  input  I0
);

  wire and_1_out, and_2_out, and_3_out, instruction_register_1_ir2, not_2_out, not_3_out;
  wire [1:0] instruction_register_1_ir0;
  wire [3:0] fourbit_alu_1_alu0, Register_A_out0, Register_B_out0;

  instruction_register instruction_register_1 (
    .clk(X), .I0(I0), .I1(I1), .I2(I2), .IR0(instruction_register_1_ir0[0]),
    .IR1(instruction_register_1_ir0[1]), .IR2(instruction_register_1_ir2));
  // NOT_Gate not_1 has open pins: in=instruction_register_1_ir2, out=open
  not not_2 (not_2_out, instruction_register_1_ir0[0]);
  not not_3 (not_3_out, instruction_register_1_ir0[1]);
  // NOT_Gate not_4 has open pins: in=instruction_register_1_ir2, out=open
  buf and_1 (and_1_out, Y);  // AND_Gate
  and and_2 (and_2_out, not_2_out, not_3_out, instruction_register_1_ir2);
  buf and_3 (and_3_out, Z);  // AND_Gate
  vcvs_register Register_A (
    .clk(and_1_out), .clr(and_2_out), .in0(A_in[0]), .in1(A_in[1]), .in2(A_in[2]), .in3(A_in[3]),
    .out0(Register_A_out0[0]), .out1(Register_A_out0[1]), .out2(Register_A_out0[2]), .out3(Register_A_out0[3]));
  vcvs_register Register_B (
    .clk(and_3_out), .clr(and_2_out), .in0(fourbit_alu_1_alu0[0]), .in1(fourbit_alu_1_alu0[1]),
    .in2(fourbit_alu_1_alu0[2]), .in3(fourbit_alu_1_alu0[3]), .out0(Register_B_out0[0]),
    .out1(Register_B_out0[1]), .out2(Register_B_out0[2]), .out3(Register_B_out0[3]));
  fourbit_alu fourbit_alu_1 (
    .A(Register_A_out0), .B(Register_B_out0), .S(instruction_register_1_ir0), .alu3(fourbit_alu_1_alu0[3]),
    .alu2(fourbit_alu_1_alu0[2]), .alu1(fourbit_alu_1_alu0[1]), .alu0(fourbit_alu_1_alu0[0]));  // open: C

  // Notes on the sheet:
  //   000-NOT
  //   001-OR
  //   010-AND
  //   011-ADD
  //   100-CLR
  //   should NOT in the ALU read from the A or B register?
  //   How should we directly put a value into the B register like in the second instruction?
  //   The diagram has us AND notIR2 and the clock for the registers, why?
  //   We can't clear the registers if we do that
endmodule

module vcvs_register (
  input  clk,
  input  clr,
  input  in0,
  input  in1,
  input  in2,
  input  in3,
  output out0,
  output out1,
  output out2,
  output out3
);

  wire and_1_out, and_2_out, and_3_out, and_4_out, not_1_out;

  not not_1 (not_1_out, clr);
  and and_1 (and_1_out, not_1_out, in0);
  and and_2 (and_2_out, not_1_out, in1);
  and and_3 (and_3_out, not_1_out, in2);
  and and_4 (and_4_out, not_1_out, in3);
  d_flip_flop d_flip_flop_1 (.D(and_1_out), .clk(clk), .Q(out0));  // open: notQ
  d_flip_flop d_flip_flop_2 (.D(and_2_out), .clk(clk), .Q(out1));  // open: notQ
  d_flip_flop d_flip_flop_3 (.D(and_3_out), .clk(clk), .Q(out2));  // open: notQ
  d_flip_flop d_flip_flop_4 (.D(and_4_out), .clk(clk), .Q(out3));  // open: notQ
endmodule

module instruction_register (
  input  clk,
  input  I0,
  input  I1,
  input  I2,
  output IR0,
  output IR1,
  output IR2
);

  d_flip_flop d_flip_flop_1 (.D(I0), .clk(clk), .Q(IR0));  // open: notQ
  d_flip_flop d_flip_flop_2 (.D(I1), .clk(clk), .Q(IR1));  // open: notQ
  d_flip_flop d_flip_flop_3 (.D(I2), .clk(clk), .Q(IR2));  // open: notQ
endmodule

module clocked_sr (
  input  S,
  input  clk,
  input  R,
  output Q,
  output notQ
);

  wire and_1_out, and_2_out;

  and and_1 (and_1_out, S, clk);
  and and_2 (and_2_out, clk, R);
  nor nor_1 (notQ, and_1_out, Q);
  nor nor_2 (Q, notQ, and_2_out);
endmodule

module d_latch (
  input  D,
  input  clk,
  output Q,
  output notQ
);

  wire not_1_out;

  not not_1 (not_1_out, D);
  clocked_sr clocked_sr_1 (.S(D), .clk(clk), .R(not_1_out), .Q(Q), .notQ(notQ));
endmodule

module d_flip_flop (
  input  D,
  input  clk,
  output Q,
  output notQ
);

  wire d_latch_1_notq, d_latch_1_q, not_1_out;

  not not_1 (not_1_out, clk);
  d_latch d_latch_1 (.D(D), .clk(clk), .Q(d_latch_1_q), .notQ(d_latch_1_notq));
  clocked_sr clocked_sr_1 (.S(d_latch_1_q), .clk(not_1_out), .R(d_latch_1_notq), .Q(Q), .notQ(notQ));
endmodule
