// Logisim project prelab_Q3.circ as structural Verilog: 2 circuits, main circuit main
module main (
  input  P3,
  input  P2,
  input  P1,
  input  P0,
  input  Pl,
  input  MR,
  input  CPdown,
  input  CPu,
  output Q3,
  output Q2,
  output Q1,
  output Q0
);

  wire n7447_1_pin3, n7447_1_pin4, n7447_1_pin5, n7447_1_pin9, n7447_1_pin10, n7447_1_pin11, n7447_1_pin12,
       n7447_1_pin13, n7447_1_pin14, n7447_1_pin15;

  _74192 u_74192_1 (
    .pin1(P1), .pin2(Q1), .pin3(Q0), .pin4(CPdown), .pin5(CPu), .pin6(Q2), .pin7(Q3), .pin15(P0), .pin14(MR),
    .pin11(Pl), .pin10(P2), .pin9(P3));  // open: pin13, pin12
  _7_Segment_Display #(.active("false")) u_7_segment_display_1 (
    .g(n7447_1_pin14), .f(n7447_1_pin15), .a(n7447_1_pin13), .b(n7447_1_pin12), .e(n7447_1_pin9),
    .d(n7447_1_pin10), .c(n7447_1_pin11));  // open: dp
  _7447 u_7447_1 (
    .pin1(Q1), .pin2(Q2), .pin3(n7447_1_pin3), .pin4(n7447_1_pin4), .pin5(n7447_1_pin5), .pin6(Q3),
    .pin7(Q0), .pin15(n7447_1_pin15), .pin14(n7447_1_pin14), .pin13(n7447_1_pin13), .pin12(n7447_1_pin12),
    .pin11(n7447_1_pin11), .pin10(n7447_1_pin10), .pin9(n7447_1_pin9));
  // also tied to VCC on the sheet: {n7447_1_pin3, n7447_1_pin4, n7447_1_pin5}
endmodule

module sr_circuit (
  input  S,
  input  Clk,
  input  R,
  output Q,
  output not_Q
);

  wire n7400_1_pin3, n7400_1_pin6, n7400_1_pin11;

  _7400 u_7400_1 (
    .pin1(Clk), .pin2(R), .pin3(n7400_1_pin3), .pin4(n7400_1_pin3), .pin5(not_Q), .pin6(n7400_1_pin6),
    .pin13(Clk), .pin12(S), .pin11(n7400_1_pin11), .pin10(n7400_1_pin11), .pin9(n7400_1_pin6), .pin8(not_Q));

  assign Q = not_Q;
endmodule
