// Logisim project Bus_and_registers.circ as structural Verilog: 3 circuits, main circuit main
module main (
  input  [3:0] Data_in,
  input  [3:0] Load,
  input  [3:0] Enable,
  input  Clk,
  output [3:0] Main_bus
);

  wire [3:0] R0_data_out, R1_data_out, R2_data_out, R3_data_out;

  assign Main_bus = Enable[0] ? R0_data_out : 4'bz;  // Controlled_Buffer controlled_buffer_1
  Register_pt2 R0 (.Data_in(Data_in), .Clk(Clk), .Load(Load[0]), .En(Enable[0]), .Data_out(R0_data_out));
  assign Main_bus = Enable[1] ? R1_data_out : 4'bz;  // Controlled_Buffer controlled_buffer_2
  Register_pt2 R1 (.Data_in(Main_bus), .Clk(Clk), .Load(Load[1]), .En(Enable[1]), .Data_out(R1_data_out));
  Register_pt2 R2 (.Data_in(Main_bus), .Clk(Clk), .Load(Load[2]), .En(Enable[2]), .Data_out(R2_data_out));
  Register_pt2 R3 (.Data_in(Main_bus), .Clk(Clk), .Load(Load[3]), .En(Enable[3]), .Data_out(R3_data_out));
  assign Main_bus = Enable[2] ? R2_data_out : 4'bz;  // Controlled_Buffer controlled_buffer_3
  assign Main_bus = Enable[3] ? R3_data_out : 4'bz;  // Controlled_Buffer controlled_buffer_4
endmodule

module Register_1 (
  input  [3:0] Data_in,
  input  Clk,
  input  Load,
  input  En,
  output [3:0] Data_out
);

  wire and_1_out, multiplexer_1_out, multiplexer_2_out, multiplexer_3_out, multiplexer_4_out, not_1_out,
       not_2_out, not_3_out, not_4_out;

  and and_1 (and_1_out, Load, En);
  Multiplexer multiplexer_1 (.in0(Data_out[0]), .in1(Data_in[0]), .out(multiplexer_1_out), .sel(and_1_out));
  Multiplexer multiplexer_2 (.in0(Data_out[1]), .in1(Data_in[1]), .out(multiplexer_2_out), .sel(and_1_out));
  Multiplexer multiplexer_3 (.in0(Data_out[2]), .in1(Data_in[2]), .out(multiplexer_3_out), .sel(and_1_out));
  Multiplexer multiplexer_4 (.in0(Data_out[3]), .in1(Data_in[3]), .out(multiplexer_4_out), .sel(and_1_out));
  J_K_Flip_Flop j_k_ff_1 (.J(multiplexer_1_out), .K(not_1_out), .clk(Clk), .Q(Data_out[0]));  // open: Qn, preset, reset
  not not_1 (not_1_out, multiplexer_1_out);
  J_K_Flip_Flop j_k_ff_2 (.J(multiplexer_2_out), .K(not_2_out), .clk(Clk), .Q(Data_out[1]));  // open: Qn, preset, reset
  not not_2 (not_2_out, multiplexer_2_out);
  J_K_Flip_Flop j_k_ff_3 (.J(multiplexer_3_out), .K(not_3_out), .clk(Clk), .Q(Data_out[2]));  // open: Qn, preset, reset
  not not_3 (not_3_out, multiplexer_3_out);
  J_K_Flip_Flop j_k_ff_4 (.J(multiplexer_4_out), .K(not_4_out), .clk(Clk), .Q(Data_out[3]));  // open: Qn, preset, reset
  not not_4 (not_4_out, multiplexer_4_out);
endmodule

module Register_pt2 (
  input  [3:0] Data_in,
  input  Clk,
  input  Load,
  input  En,
  output [3:0] Data_out
);

  wire j_k_ff_1_q, j_k_ff_2_q, j_k_ff_3_q, j_k_ff_4_q, multiplexer_1_out, multiplexer_2_out,
       multiplexer_3_out, multiplexer_4_out, not_1_out, not_2_out, not_3_out, not_4_out;

  Multiplexer multiplexer_1 (.in0(j_k_ff_1_q), .in1(Data_in[0]), .out(multiplexer_1_out), .sel(Load));
  Multiplexer multiplexer_2 (.in0(j_k_ff_2_q), .in1(Data_in[1]), .out(multiplexer_2_out), .sel(Load));
  Multiplexer multiplexer_3 (.in0(j_k_ff_3_q), .in1(Data_in[2]), .out(multiplexer_3_out), .sel(Load));
  Multiplexer multiplexer_4 (.in0(j_k_ff_4_q), .in1(Data_in[3]), .out(multiplexer_4_out), .sel(Load));
  J_K_Flip_Flop j_k_ff_1 (.J(multiplexer_1_out), .K(not_1_out), .clk(Clk), .Q(j_k_ff_1_q));  // open: Qn, preset, reset
  not not_1 (not_1_out, multiplexer_1_out);
  J_K_Flip_Flop j_k_ff_2 (.J(multiplexer_2_out), .K(not_2_out), .clk(Clk), .Q(j_k_ff_2_q));  // open: Qn, preset, reset
  not not_2 (not_2_out, multiplexer_2_out);
  J_K_Flip_Flop j_k_ff_3 (.J(multiplexer_3_out), .K(not_3_out), .clk(Clk), .Q(j_k_ff_3_q));  // open: Qn, preset, reset
  not not_3 (not_3_out, multiplexer_3_out);
  J_K_Flip_Flop j_k_ff_4 (.J(multiplexer_4_out), .K(not_4_out), .clk(Clk), .Q(j_k_ff_4_q));  // open: Qn, preset, reset
  not not_4 (not_4_out, multiplexer_4_out);
  assign Data_out[0] = En ? j_k_ff_1_q : 1'bz;  // Controlled_Buffer controlled_buffer_1
  assign Data_out[1] = En ? j_k_ff_2_q : 1'bz;  // Controlled_Buffer controlled_buffer_2
  assign Data_out[2] = En ? j_k_ff_3_q : 1'bz;  // Controlled_Buffer controlled_buffer_3
  assign Data_out[3] = En ? j_k_ff_4_q : 1'bz;  // Controlled_Buffer controlled_buffer_4
endmodule
